// Logisim project 6 Bit Register File.circ as structural Verilog: 2 circuits, main circuit main
module main (
  input  [2:0] in_1,
  input  [2:0] in_2,
  input  [2:0] in_3,
  input  [5:0] in_4,
  input  in_5,
  output [5:0] out_6,
  output [5:0] out_7
);

  wire clock_1_out;

  _6_Bit_Register_File u_6_bit_register_file_1 (
    .Write_Data(in_4), .WC(in_5), .CLK(clock_1_out), .Write_Register(in_3), .Read_Register_1(in_1),
    .Read_Register_2(in_2), .Read_Data_1(out_6), .Read_Data_2(out_7));
  Clock clock_1 (.out(clock_1_out));
endmodule

module _6_Bit_Register_File (
  input  [5:0] Write_Data,
  input  [2:0] Read_Register_1,
  input  [2:0] Write_Register,
  input  [2:0] Read_Register_2,
  input  WC,
  input  CLK,
  output [5:0] Read_Data_1,
  output [5:0] Read_Data_2
);

  wire and_1_out, decoder_1_out0, decoder_1_out1, decoder_1_out2, decoder_1_out3, decoder_1_out4,
       decoder_1_out5, decoder_1_out6, decoder_1_out7;
  wire [5:0] register_1_q, register_2_q, register_3_q, register_4_q, register_5_q, register_6_q,
       register_7_q, register_8_q;

  Decoder #(.select(3)) decoder_1 (
    .out0(decoder_1_out0), .out1(decoder_1_out1), .out2(decoder_1_out2), .out3(decoder_1_out3),
    .out4(decoder_1_out4), .out5(decoder_1_out5), .out6(decoder_1_out6), .out7(decoder_1_out7),
    .sel(Write_Register));  // open: en
  and and_1 (and_1_out, WC, CLK);
  Register #(.width(6)) register_1 (
    .D(Write_Data), .en(decoder_1_out0), .Q(register_1_q), .clk(and_1_out));  // open: clr
  Register #(.width(6)) register_2 (
    .D(Write_Data), .en(decoder_1_out1), .Q(register_2_q), .clk(and_1_out));  // open: clr
  Register #(.width(6)) register_3 (
    .D(Write_Data), .en(decoder_1_out2), .Q(register_3_q), .clk(and_1_out));  // open: clr
  Register #(.width(6)) register_4 (
    .D(Write_Data), .en(decoder_1_out3), .Q(register_4_q), .clk(and_1_out));  // open: clr
  Register #(.width(6)) register_5 (
    .D(Write_Data), .en(decoder_1_out4), .Q(register_5_q), .clk(and_1_out));  // open: clr
  Register #(.width(6)) register_6 (
    .D(Write_Data), .en(decoder_1_out5), .Q(register_6_q), .clk(and_1_out));  // open: clr
  Register #(.width(6)) register_7 (
    .D(Write_Data), .en(decoder_1_out6), .Q(register_7_q), .clk(and_1_out));  // open: clr
  Register #(.width(6)) register_8 (
    .D(Write_Data), .en(decoder_1_out7), .Q(register_8_q), .clk(and_1_out));  // open: clr
  Multiplexer #(.select(3), .width(6)) multiplexer_1 (
    .in0(register_1_q), .in1(register_2_q), .in2(register_3_q), .in3(register_4_q), .in4(register_5_q),
    .in5(register_6_q), .in6(register_7_q), .in7(register_8_q), .out(Read_Data_1), .sel(Read_Register_1));  // open: en
  Multiplexer #(.select(3), .width(6)) multiplexer_2 (
    .in0(register_1_q), .in1(register_2_q), .in2(register_3_q), .in3(register_4_q), .in4(register_5_q),
    .in5(register_6_q), .in6(register_7_q), .in7(register_8_q), .out(Read_Data_2), .sel(Read_Register_2));  // open: en

  // Notes on the sheet:
  //   Syed Mozahidul Islam
endmodule
