// Logisim project LAB2 Two Bit arith unit.circ as structural Verilog: 1 circuit, main circuit Syed Mozahidul Islam
module Syed_Mozahidul_Islam (
  input  [1:0] S0__S1,
  input  Cin,
  input  A0,
  input  A1,
  input  B0,
  input  B1,
  input  in_7,
  input  in_8,
  output out_9,
  output out_10,
  output out_11
);

  wire adder_2_cout, multiplexer_1_out, multiplexer_2_out, not_1_out, not_2_out;

  not not_1 (not_1_out, B1);
  not not_2 (not_2_out, B0);
  Multiplexer #(.select(2)) multiplexer_1 (
    .in0(B0), .in1(not_2_out), .in2(in_7), .in3(in_8), .out(multiplexer_1_out), .sel(S0__S1));  // open: en
  Multiplexer #(.select(2)) multiplexer_2 (
    .in0(B1), .in1(not_1_out), .in2(in_7), .in3(in_7), .out(multiplexer_2_out), .sel(S0__S1));  // open: en
  Adder #(.width(1)) adder_1 (.a(A1), .b(multiplexer_2_out), .out(out_10), .cin(adder_2_cout), .cout(out_11));
  Adder #(.width(1)) adder_2 (.a(A0), .b(multiplexer_1_out), .out(out_9), .cin(Cin), .cout(adder_2_cout));

  // Notes on the sheet:
  //   Shaikh Farhana Supti
  //   2111672642 Sec 4 Group 4 
  //   D0
  //   D1
  //   Cout
endmodule
