// Logisim project LAB3 4Bit Binary mul unit .circ as structural Verilog: 1 circuit, main circuit main
module main (
  input  SR,
  input  I4,
  input  I3,
  input  I2,
  input  SL,
  input  I1,
  input  [1:0] Select_Bits,
  output A4,
  output A3,
  output A2,
  output A1
);

  wire button_1_out, clock_1_out, multiplexer_1_out, multiplexer_2_out, multiplexer_3_out, multiplexer_4_out;

  Multiplexer #(.select(2)) multiplexer_1 (
    .in0(A4), .in1(SR), .in2(A3), .in3(I4), .out(multiplexer_1_out), .sel(Select_Bits));  // open: en
  Multiplexer #(.select(2)) multiplexer_2 (
    .in0(A3), .in1(A4), .in2(A2), .in3(I3), .out(multiplexer_2_out), .sel(Select_Bits));  // open: en
  Multiplexer #(.select(2)) multiplexer_3 (
    .in0(A2), .in1(A3), .in2(A1), .in3(I2), .out(multiplexer_3_out), .sel(Select_Bits));  // open: en
  Multiplexer #(.select(2)) multiplexer_4 (
    .in0(A1), .in1(A2), .in2(SL), .in3(I1), .out(multiplexer_4_out), .sel(Select_Bits));  // open: en
  Clock clock_1 (.out(clock_1_out));
  D_Flip_Flop d_ff_1 (.clk(clock_1_out), .D(multiplexer_1_out), .Q(A4), .reset(button_1_out));  // open: Qn, preset, en
  D_Flip_Flop d_ff_2 (.clk(clock_1_out), .D(multiplexer_2_out), .Q(A3), .reset(button_1_out));  // open: Qn, preset, en
  D_Flip_Flop d_ff_3 (.clk(clock_1_out), .D(multiplexer_3_out), .Q(A2), .reset(button_1_out));  // open: Qn, preset, en
  D_Flip_Flop d_ff_4 (.clk(clock_1_out), .D(multiplexer_4_out), .Q(A1), .reset(button_1_out));  // open: Qn, preset, en
  Button button_1 (.out(button_1_out));

  // Notes on the sheet:
  //   Shaikh Farhana Supti
  //   2112266642
endmodule
