// Logisim project LAB6 Design of ALU.circ as structural Verilog: 4 circuits, main circuit main
module main (
  input  [2:0] in_1,
  input  [2:0] in_2,
  input  [2:0] in_3,
  input  in_4,
  input  [1:0] in_5,
  input  in_6,
  output out_7
);

  wire clock_1_out;
  wire [5:0] n6_bit_alu_1_out_5, n6_bit_register_file_1_rd1, n6_bit_register_file_1_rd2;

  _6_Bit_Register_File u_6_bit_register_file_1 (
    .WD(n6_bit_alu_1_out_5), .WC(in_6), .CLK(clock_1_out), .RD1(n6_bit_register_file_1_rd1),
    .RD2(n6_bit_register_file_1_rd2), .WR(in_3), .RR1(in_1), .RR2(in_2));
  Clock clock_1 (.out(clock_1_out));
  _6_Bit_ALU u_6_bit_alu_1 (
    .in_3(in_4), .in_4(in_5), .out_5(n6_bit_alu_1_out_5), .out_6(out_7), .in_1(n6_bit_register_file_1_rd2),
    .in_2(n6_bit_register_file_1_rd1));
endmodule

module _1_Bit_ALU (
  input  in_1,
  input  in_2,
  input  Cin,
  input  [1:0] in_4,
  output out_5,
  output out_6
);

  wire adder_1_cout, adder_1_out, and_1_out, or_1_out, subtractor_1_bout, subtractor_1_out;

  and and_1 (and_1_out, in_1, in_2);
  or or_1 (or_1_out, in_1, in_2);
  Adder #(.width(1)) adder_1 (.a(in_1), .b(in_2), .out(adder_1_out), .cin(Cin), .cout(adder_1_cout));
  Subtractor #(.width(1)) subtractor_1 (
    .a(in_1), .b(in_2), .out(subtractor_1_out), .bin(Cin), .bout(subtractor_1_bout));
  Multiplexer #(.select(2)) multiplexer_1 (
    .in0(and_1_out), .in1(or_1_out), .in2(adder_1_out), .in3(subtractor_1_out), .out(out_5), .sel(in_4));  // open: en
  Multiplexer multiplexer_2 (.in0(adder_1_cout), .in1(subtractor_1_bout), .out(out_6), .sel(in_4[0]), .en(in_4[1]));
endmodule

module _6_Bit_ALU (
  input  [5:0] in_1,
  input  [5:0] in_2,
  input  in_3,
  input  [1:0] in_4,
  output [5:0] out_5,
  output out_6
);

  wire n1_bit_alu_1_out_6, n1_bit_alu_2_out_6, n1_bit_alu_3_out_6, n1_bit_alu_4_out_6, n1_bit_alu_5_out_6;

  _1_Bit_ALU u_1_bit_alu_1 (
    .in_1(in_1[0]), .in_2(in_2[0]), .Cin(in_3), .in_4(in_4), .out_5(out_5[0]), .out_6(n1_bit_alu_1_out_6));
  _1_Bit_ALU u_1_bit_alu_2 (
    .in_1(in_1[1]), .in_2(in_2[1]), .Cin(n1_bit_alu_1_out_6), .in_4(in_4), .out_5(out_5[1]),
    .out_6(n1_bit_alu_2_out_6));
  _1_Bit_ALU u_1_bit_alu_3 (
    .in_1(in_1[2]), .in_2(in_2[2]), .Cin(n1_bit_alu_2_out_6), .in_4(in_4), .out_5(out_5[2]),
    .out_6(n1_bit_alu_3_out_6));
  _1_Bit_ALU u_1_bit_alu_4 (
    .in_1(in_1[3]), .in_2(in_2[3]), .Cin(n1_bit_alu_3_out_6), .in_4(in_4), .out_5(out_5[3]),
    .out_6(n1_bit_alu_4_out_6));
  _1_Bit_ALU u_1_bit_alu_5 (
    .in_1(in_1[4]), .in_2(in_2[4]), .Cin(n1_bit_alu_4_out_6), .in_4(in_4), .out_5(out_5[4]),
    .out_6(n1_bit_alu_5_out_6));
  _1_Bit_ALU u_1_bit_alu_6 (
    .in_1(in_1[5]), .in_2(in_2[5]), .Cin(n1_bit_alu_5_out_6), .in_4(in_4), .out_5(out_5[5]), .out_6(out_6));
endmodule

module _6_Bit_Register_File (
  input  [5:0] WD,
  input  [2:0] RR1,
  input  [2:0] WR,
  input  [2:0] RR2,
  input  WC,
  input  CLK,
  output [5:0] RD1,
  output [5:0] RD2
);

  wire and_1_out, decoder_1_out0, decoder_1_out1, decoder_1_out2, decoder_1_out3, decoder_1_out4,
       decoder_1_out5, decoder_1_out6, decoder_1_out7;
  wire [5:0] register_1_q, register_2_q, register_3_q, register_4_q, register_5_q, register_6_q,
       register_7_q, register_8_q;

  Decoder #(.select(3)) decoder_1 (
    .out0(decoder_1_out0), .out1(decoder_1_out1), .out2(decoder_1_out2), .out3(decoder_1_out3),
    .out4(decoder_1_out4), .out5(decoder_1_out5), .out6(decoder_1_out6), .out7(decoder_1_out7), .sel(WR));  // open: en
  and and_1 (and_1_out, WC, CLK);
  Register #(.width(6)) register_1 (.D(WD), .en(decoder_1_out0), .Q(register_1_q), .clk(and_1_out));  // open: clr
  Register #(.width(6)) register_2 (.D(WD), .en(decoder_1_out1), .Q(register_2_q), .clk(and_1_out));  // open: clr
  Register #(.width(6)) register_3 (.D(WD), .en(decoder_1_out2), .Q(register_3_q), .clk(and_1_out));  // open: clr
  Register #(.width(6)) register_4 (.D(WD), .en(decoder_1_out3), .Q(register_4_q), .clk(and_1_out));  // open: clr
  Register #(.width(6)) register_5 (.D(WD), .en(decoder_1_out4), .Q(register_5_q), .clk(and_1_out));  // open: clr
  Register #(.width(6)) register_6 (.D(WD), .en(decoder_1_out5), .Q(register_6_q), .clk(and_1_out));  // open: clr
  Register #(.width(6)) register_7 (.D(WD), .en(decoder_1_out6), .Q(register_7_q), .clk(and_1_out));  // open: clr
  Register #(.width(6)) register_8 (.D(WD), .en(decoder_1_out7), .Q(register_8_q), .clk(and_1_out));  // open: clr
  Multiplexer #(.select(3), .width(6)) multiplexer_1 (
    .in0(register_1_q), .in1(register_2_q), .in2(register_3_q), .in3(register_4_q), .in4(register_5_q),
    .in5(register_6_q), .in6(register_7_q), .in7(register_8_q), .out(RD1), .sel(RR1));  // open: en
  Multiplexer #(.select(3), .width(6)) multiplexer_2 (
    .in0(register_1_q), .in1(register_2_q), .in2(register_3_q), .in3(register_4_q), .in4(register_5_q),
    .in5(register_6_q), .in6(register_7_q), .in7(register_8_q), .out(RD2), .sel(RR2));  // open: en
endmodule
