// Logisim project LAB7 Single Cycle Data Path.circ as structural Verilog
module _1_Bit_ALU (
  input  A,
  input  B,
  input  C_in,
  input  [1:0] Opcode,
  output F,
  output C_out
);

  wire adder_1_cout, adder_1_out, and_1_out, or_1_out, subtractor_1_bout, subtractor_1_out;

  and and_1 (and_1_out, A, B);
  or or_1 (or_1_out, A, B);
  Adder #(.width(1)) adder_1 (.a(A), .b(B), .out(adder_1_out), .cin(C_in), .cout(adder_1_cout));
  Subtractor #(.width(1)) subtractor_1 (.a(A), .b(B), .out(subtractor_1_out), .bin(C_in), .bout(subtractor_1_bout));
  Multiplexer #(.select(2)) multiplexer_1 (
    .in0(and_1_out), .in1(or_1_out), .in2(adder_1_out), .in3(subtractor_1_out), .out(F), .sel(Opcode));  // open: en
  Multiplexer multiplexer_2 (.in0(adder_1_cout), .in1(subtractor_1_bout), .out(C_out), .sel(Opcode[0]), .en(Opcode[1]));
endmodule

module _6_Bit_ALU (
  input  [5:0] A,
  input  [5:0] B,
  input  C_in,
  input  [1:0] Opcode,
  output [5:0] F,
  output C_out
);

  wire n1_bit_alu_1_c_out, n1_bit_alu_2_c_out, n1_bit_alu_3_c_out, n1_bit_alu_4_c_out, n1_bit_alu_5_c_out;

  _1_Bit_ALU u_1_bit_alu_1 (.A(A[0]), .B(B[0]), .C_in(C_in), .Opcode(Opcode), .F(F[0]), .C_out(n1_bit_alu_1_c_out));
  _1_Bit_ALU u_1_bit_alu_2 (
    .A(A[1]), .B(B[1]), .C_in(n1_bit_alu_1_c_out), .Opcode(Opcode), .F(F[1]), .C_out(n1_bit_alu_2_c_out));
  _1_Bit_ALU u_1_bit_alu_3 (
    .A(A[2]), .B(B[2]), .C_in(n1_bit_alu_2_c_out), .Opcode(Opcode), .F(F[2]), .C_out(n1_bit_alu_3_c_out));
  _1_Bit_ALU u_1_bit_alu_4 (
    .A(A[3]), .B(B[3]), .C_in(n1_bit_alu_3_c_out), .Opcode(Opcode), .F(F[3]), .C_out(n1_bit_alu_4_c_out));
  _1_Bit_ALU u_1_bit_alu_5 (
    .A(A[4]), .B(B[4]), .C_in(n1_bit_alu_4_c_out), .Opcode(Opcode), .F(F[4]), .C_out(n1_bit_alu_5_c_out));
  _1_Bit_ALU u_1_bit_alu_6 (.A(A[5]), .B(B[5]), .C_in(n1_bit_alu_5_c_out), .Opcode(Opcode), .F(F[5]), .C_out(C_out));
endmodule

module _6_Bit_Register_File (
  input  [5:0] WD,
  input  [2:0] RR1,
  input  [2:0] WR,
  input  [2:0] RR2,
  input  WC,
  input  CLK,
  output [5:0] RD1,
  output [5:0] RD2
);

  wire and_1_out, decoder_1_out0, decoder_1_out1, decoder_1_out2, decoder_1_out3, decoder_1_out4,
       decoder_1_out5, decoder_1_out6, decoder_1_out7;
  wire [5:0] register_1_q, register_2_q, register_3_q, register_4_q, register_5_q, register_6_q,
       register_7_q, register_8_q;

  Decoder #(.select(3)) decoder_1 (
    .out0(decoder_1_out0), .out1(decoder_1_out1), .out2(decoder_1_out2), .out3(decoder_1_out3),
    .out4(decoder_1_out4), .out5(decoder_1_out5), .out6(decoder_1_out6), .out7(decoder_1_out7), .sel(WR));  // open: en
  and and_1 (and_1_out, WC, CLK);
  Register #(.width(6)) register_1 (.D(WD), .en(decoder_1_out0), .Q(register_1_q), .clk(and_1_out));  // open: clr
  Register #(.width(6)) register_2 (.D(WD), .en(decoder_1_out1), .Q(register_2_q), .clk(and_1_out));  // open: clr
  Register #(.width(6)) register_3 (.D(WD), .en(decoder_1_out2), .Q(register_3_q), .clk(and_1_out));  // open: clr
  Register #(.width(6)) register_4 (.D(WD), .en(decoder_1_out3), .Q(register_4_q), .clk(and_1_out));  // open: clr
  Register #(.width(6)) register_5 (.D(WD), .en(decoder_1_out4), .Q(register_5_q), .clk(and_1_out));  // open: clr
  Register #(.width(6)) register_6 (.D(WD), .en(decoder_1_out5), .Q(register_6_q), .clk(and_1_out));  // open: clr
  Register #(.width(6)) register_7 (.D(WD), .en(decoder_1_out6), .Q(register_7_q), .clk(and_1_out));  // open: clr
  Register #(.width(6)) register_8 (.D(WD), .en(decoder_1_out7), .Q(register_8_q), .clk(and_1_out));  // open: clr
  Multiplexer #(.select(3), .width(6)) multiplexer_1 (
    .in0(register_1_q), .in1(register_2_q), .in2(register_3_q), .in3(register_4_q), .in4(register_5_q),
    .in5(register_6_q), .in6(register_7_q), .in7(register_8_q), .out(RD1), .sel(RR1));  // open: en
  Multiplexer #(.select(3), .width(6)) multiplexer_2 (
    .in0(register_1_q), .in1(register_2_q), .in2(register_3_q), .in3(register_4_q), .in4(register_5_q),
    .in5(register_6_q), .in6(register_7_q), .in7(register_8_q), .out(RD2), .sel(RR2));  // open: en
endmodule

// Syed Mozahidul Islam
module Single_Cycle_Datapath_for_R_type_instruction (
  input  in_1,
  input  in_2,
  output out_3
);

  wire clock_1_out;
  wire [1:0] rom_1_data_2;
  wire [4:0] adder_1_out, register_1_q;
  wire [5:0] n6_bit_alu_1_f, n6_bit_register_file_1_rd1, n6_bit_register_file_1_rd2;
  wire [8:0] rom_1_data;

  Register #(.width(5)) register_1 (.D(adder_1_out), .Q(register_1_q), .clk(clock_1_out));  // open: en, clr
  Adder #(.width(5)) adder_1 (.a(5'b00001), .b(register_1_q), .out(adder_1_out));  // open: cin, cout
  ROM #(.addrWidth(5), .dataWidth(11)) rom_1 (.addr(register_1_q), .data({rom_1_data_2, rom_1_data}));  // open: sel
  _6_Bit_Register_File u_6_bit_register_file_1 (
    .WD(n6_bit_alu_1_f), .WC(in_2), .CLK(clock_1_out), .RD1(n6_bit_register_file_1_rd1),
    .RD2(n6_bit_register_file_1_rd2), .WR(rom_1_data[2:0]), .RR1(rom_1_data[8:6]), .RR2(rom_1_data[5:3]));
  Clock clock_1 (.out(clock_1_out));
  _6_Bit_ALU u_6_bit_alu_1 (
    .C_in(in_1), .Opcode(rom_1_data_2), .A(n6_bit_register_file_1_rd1), .B(n6_bit_register_file_1_rd2),
    .C_out(out_3), .F(n6_bit_alu_1_f));

  // Notes on the sheet:
  //   contents of rom_1 (hex, n*v repeats v):
  //   40c 9d 72f
  //   Syed Mozahidul Islam
endmodule
